// Digital circuit jelly-glues.dig as structural Verilog
module jelly_glues (
  input  T0,
  input  T1,
  input  T2,
  input  T3,
  output OE6,
  output OE7,
  output CS5,
  output CS4
);

  wire and_1_out, and_2_out, and_3_out, and_4_out, and_5_out, and_6_out, and_7_out, nand_1_out, nand_2_out,
       nand_3_out, nand_4_out, nand_5_out, nand_6_out, or_1_out, or_2_out, or_3_out, or_4_out, or_5_out,
       or_7_out;

  nand nand_1 (nand_1_out, T2, T2);
  nand nand_2 (nand_2_out, T3, T3);
  and and_1 (and_1_out, T2, T3);
  and and_2 (and_2_out, T0, T1);
  or or_1 (or_1_out, T0, T1);
  or or_2 (or_2_out, T2, T3);
  or or_3 (or_3_out, nand_1_out, T3);
  or or_4 (or_4_out, T2, nand_2_out);
  nand nand_3 (nand_3_out, or_2_out, or_2_out);
  nand nand_4 (nand_4_out, or_3_out, or_3_out);
  nand nand_5 (nand_5_out, or_4_out, or_4_out);
  nand nand_6 (nand_6_out, or_1_out, or_1_out);
  and and_3 (and_3_out, or_1_out, nand_3_out);
  and and_4 (and_4_out, or_1_out, nand_4_out);
  or or_5 (or_5_out, and_2_out, nand_6_out);
  and and_5 (and_5_out, nand_6_out, nand_4_out);
  and and_6 (and_6_out, nand_6_out, and_1_out);
  and and_7 (and_7_out, nand_6_out, nand_4_out);
  and and_8 (CS4, or_5_out, nand_5_out);
  or or_6 (CS5, and_6_out, and_7_out);
  or or_7 (or_7_out, and_3_out, and_5_out);
  nand nand_7 (OE6, or_7_out, or_7_out);
  nand nand_8 (OE7, and_4_out, and_4_out);

  // Notes on the sheet:
  //   5, 6, 7
  //   8, 9, 10
endmodule
