// Digital circuit jelly-seven.dig as structural Verilog
module jelly_seven (
  input  clock,
  input  halt,
  input  D0,
  input  D1,
  input  D2,
  input  D3,
  input  D4,
  input  D5,
  input  D6,
  input  D7,
  output D0_2,
  output D1_2,
  output D2_2,
  output D3_2,
  output D4_2,
  output D5_2,
  output D6_2,
  output D7_2,
  output zero,
  output ce6,
  output oe4,
  output m2,
  output m1,
  output A0,
  output A1,
  output A2,
  output A3,
  output A4,
  output A5,
  output A6,
  output A7
);

  wire not_1_out, U1_p16, U1_p19, U1_p20, U1_p21, U6_p14, U6_p15, U6_p18, U7_p2, U7_p3, U7_p4, U7_p5, U7_p6,
       U7_p7, U7_p8, U7_p9, U7_p10, U7_p11, U7_p12, U7_p13, U7_p14, U7_p15, U7_p16, U7_p17, U7_p18,
       u8_2_pin3, u8_2_pin6, u8_2_pin8, u8_2_pin13, U8_pin10, U8_pin20, u9_2_pin3, u9_2_pin6, U9_pin1,
       U9_pin10, U9_pin11, U9_pin20, U10_pin1, U10_pin11, U10_pin12, U10_pin13, U10_pin14, U10_pin15,
       U10_pin16, U10_pin17, U10_pin18, U10_pin19, U11_pin5, U11_pin11, U11_pin12, U11_pin13, U11_pin14;
  wire [2:0] U1_p11, U1_p13, U2_p12, U3_p12, U5_p9;
  wire [7:0] U6_p9, U8_pin9, U9_pin3, U9_pin12, U11_pin3;
  wire [7:3] U5_p20, U7_p1, U8_pin11;
  wire [7:7] U1_p1;

  _74273 U9 (
    .pin1(U9_pin1), .pin2(U9_pin12[0]), .pin3(U9_pin3[0]), .pin4(U9_pin3[1]), .pin5(U9_pin12[1]),
    .pin6(U9_pin12[2]), .pin7(U9_pin3[2]), .pin8(U9_pin3[3]), .pin9(U9_pin12[3]), .pin10(U9_pin10),
    .pin11(U9_pin11), .pin12(U9_pin12[4]), .pin13(U9_pin3[4]), .pin14(U9_pin3[5]), .pin15(U9_pin12[5]),
    .pin16(U9_pin12[6]), .pin17(U9_pin3[6]), .pin18(U9_pin3[7]), .pin19(U9_pin12[7]), .pin20(U9_pin20));
  _74193 U11 (
    .pin1(U9_pin3[1]), .pin2(U11_pin3[1]), .pin3(U11_pin3[0]), .pin4(U9_pin10), .pin5(U11_pin5),
    .pin6(U11_pin3[2]), .pin7(U11_pin3[3]), .pin8(U9_pin10), .pin9(U9_pin3[3]), .pin10(U9_pin3[2]),
    .pin11(U11_pin11), .pin12(U11_pin12), .pin13(U11_pin13), .pin14(U11_pin14), .pin15(U9_pin3[0]),
    .pin16(U9_pin20));
  _74193 U12 (
    .pin1(U9_pin3[5]), .pin2(U11_pin3[5]), .pin3(U11_pin3[4]), .pin4(U11_pin13), .pin5(U11_pin12),
    .pin6(U11_pin3[6]), .pin7(U11_pin3[7]), .pin8(U9_pin10), .pin9(U9_pin3[7]), .pin10(U9_pin3[6]),
    .pin11(U11_pin11), .pin14(U11_pin14), .pin15(U9_pin3[4]), .pin16(U9_pin20));  // open: pin12, pin13
  // _28c16 U6: pin names not known; wires that end beside it: U9_pin12[7], U9_pin12[6], U9_pin12[5], U9_pin12[4], U9_pin12[3], U9_pin12[2], U9_pin12[1], U9_pin12[0], U6_p9[0], U6_p9[1], U6_p9[2], U9_pin10, U9_pin20, U6_p14, U6_p15, U9_pin20, U9_pin10, U6_p18, U9_pin10, U6_p9[7], U6_p9[6], U6_p9[5]
  _74273 U8 (
    .pin1(U8_pin11[4]), .pin2(U8_pin9[0]), .pin3(U9_pin3[0]), .pin4(U9_pin3[1]), .pin5(U8_pin9[1]),
    .pin6(U8_pin9[2]), .pin7(U9_pin3[2]), .pin8(U9_pin3[3]), .pin9(U8_pin9[3]), .pin10(U8_pin10),
    .pin11(U8_pin11[3]), .pin12(U8_pin9[4]), .pin13(U9_pin3[4]), .pin14(U9_pin3[5]), .pin15(U8_pin9[5]),
    .pin16(U8_pin9[6]), .pin17(U9_pin3[6]), .pin18(U9_pin3[7]), .pin19(U8_pin9[7]), .pin20(U8_pin20));
  _7432 u8_2 (
    .pin1(U9_pin3[0]), .pin2(U9_pin3[1]), .pin3(u8_2_pin3), .pin4(U9_pin3[2]), .pin5(U9_pin3[3]),
    .pin6(u8_2_pin6), .pin7(1'b0), .pin8(u8_2_pin8), .pin9(u8_2_pin6), .pin10(u8_2_pin3), .pin11(zero),
    .pin12(u8_2_pin8), .pin13(u8_2_pin13), .pin14(1'b1));
  _7432 u9_2 (
    .pin1(U9_pin3[4]), .pin2(U9_pin3[5]), .pin3(u9_2_pin3), .pin4(U9_pin3[6]), .pin5(U9_pin3[7]),
    .pin6(u9_2_pin6), .pin7(1'b0), .pin8(u8_2_pin13), .pin9(u9_2_pin6), .pin10(u9_2_pin3), .pin12(1'b1),
    .pin13(1'b1), .pin14(1'b1));  // open: pin11
  LED led_1 (.in(zero));
  // _28c16 U1: pin names not known; wires that end beside it: U1_p1[7], U6_p9[2], U6_p9[1], U6_p9[0], U11_pin3[3], U11_pin3[2], U11_pin3[1], U11_pin3[0], U1_p11[0], U1_p11[1], U1_p11[2], 1'b1, U1_p13[0], U1_p13[1], 1'b1, U1_p16, U1_p13[2], U1_p16, U1_p19, U1_p20, U1_p21, U1_p16
  // _28c16 U2: pin names not known; wires that end beside it: U1_p16, U1_p1[7], U6_p9[2], U6_p9[1], U6_p9[0], U11_pin3[3], U11_pin3[2], U11_pin3[1], U11_pin3[0], U2_p12[0], U2_p12[1], U2_p12[2], 1'b1, U1_p13[0], U1_p13[1], 1'b1, U1_p16, U1_p13[2], U1_p16, U8_pin11[7], U8_pin11[6], U8_pin11[5]
  // _28c16 U3: pin names not known; wires that end beside it: U1_p16, U1_p1[7], U6_p9[2], U6_p9[1], U6_p9[0], U11_pin3[3], U11_pin3[2], U11_pin3[1], U11_pin3[0], U3_p12[0], U3_p12[1], U3_p12[2], U1_p16, 1'b1, U1_p13[0], U1_p13[1], 1'b1, U1_p16, U1_p13[2], U1_p16, U7_p1[7], U7_p1[6], U7_p1[5]
  // _28c16 U5: pin names not known; wires that end beside it: U8_pin9[7], U8_pin9[6], U8_pin9[5], U8_pin9[4], U8_pin9[3], U8_pin9[2], U8_pin9[1], U8_pin9[0], U5_p9[0], U5_p9[1], U5_p9[2], U8_pin10, U8_pin20, U2_p12[0], U2_p12[1], U8_pin20, U8_pin10, U2_p12[2], U8_pin10, U5_p20[7], U5_p20[6], U5_p20[5]
  _74574 U9_3 (
    .pin1(U8_pin11[6]), .pin2(U5_p9[0]), .pin3(U5_p9[1]), .pin4(U5_p9[2]), .pin5(U5_p20[3]),
    .pin6(U5_p20[4]), .pin7(U5_p20[5]), .pin8(U5_p20[6]), .pin9(U5_p20[7]), .pin10(U8_pin10),
    .pin11(U8_pin11[5]), .pin12(U9_pin3[7]), .pin13(U9_pin3[6]), .pin14(U9_pin3[5]), .pin15(U9_pin3[4]),
    .pin16(U9_pin3[3]), .pin17(U9_pin3[2]), .pin18(U9_pin3[1]), .pin19(U9_pin3[0]), .pin20(U8_pin20));
  LED led_2 (.in(D1));
  LED led_3 (.in(D0));
  PullDown pulldown_1 (.out(D0));
  PullDown pulldown_2 (.out(D1));
  LED led_4 (.in(D3));
  LED led_5 (.in(D2));
  PullDown pulldown_3 (.out(D2));
  PullDown pulldown_4 (.out(D3));
  LED led_6 (.in(D5));
  LED led_7 (.in(D4));
  PullDown pulldown_5 (.out(D4));
  PullDown pulldown_6 (.out(D5));
  LED led_8 (.in(D7));
  LED led_9 (.in(D6));
  PullDown pulldown_7 (.out(D6));
  PullDown pulldown_8 (.out(D7));
  LED led_10 (.in(U9_pin3[0]));
  PullDown pulldown_9 (.out(U9_pin3[0]));
  LED led_11 (.in(U9_pin3[2]));
  LED led_12 (.in(U9_pin3[1]));
  PullDown pulldown_10 (.out(U9_pin3[1]));
  PullDown pulldown_11 (.out(U9_pin3[2]));
  LED led_13 (.in(U9_pin3[4]));
  LED led_14 (.in(U9_pin3[3]));
  PullDown pulldown_12 (.out(U9_pin3[3]));
  PullDown pulldown_13 (.out(U9_pin3[4]));
  LED led_15 (.in(U9_pin3[6]));
  LED led_16 (.in(U9_pin3[5]));
  PullDown pulldown_14 (.out(U9_pin3[5]));
  PullDown pulldown_15 (.out(U9_pin3[6]));
  LED led_17 (.in(U9_pin3[7]));
  PullDown pulldown_16 (.out(U9_pin3[7]));
  // _74574 U7: pin names not known; wires that end beside it: {U7_p1, U3_p12}, U7_p2, U7_p3, U7_p4, U7_p5, U7_p6, U7_p7, U7_p8, U7_p9, U7_p10, U7_p11, U7_p12, U7_p13, U7_p14, U7_p15, U7_p16, U7_p17, U7_p18, U7_p10, U7_p9
  _74245 U10 (
    .pin1(U10_pin1), .pin2(U9_pin3[0]), .pin3(U9_pin3[1]), .pin4(U9_pin3[2]), .pin5(U9_pin3[3]),
    .pin6(U9_pin3[4]), .pin7(U9_pin3[5]), .pin8(U9_pin3[6]), .pin9(U9_pin3[7]), .pin10(U7_p9),
    .pin11(U10_pin11), .pin12(U10_pin12), .pin13(U10_pin13), .pin14(U10_pin14), .pin15(U10_pin15),
    .pin16(U10_pin16), .pin17(U10_pin17), .pin18(U10_pin18), .pin19(U10_pin19), .pin20(U7_p10));
  LED led_18 (.in(m1));
  PullDown pulldown_17 (.out(m1));
  LED led_19 (.in(oe4));
  LED led_20 (.in(m2));
  PullDown pulldown_18 (.out(m2));
  PullDown pulldown_19 (.out(oe4));
  LED led_21 (.in(ce6));
  PullDown pulldown_20 (.out(ce6));
  LED led_22 (.in(clock));
  not not_1 (not_1_out, halt);
  LED led_23 (.in(not_1_out));
  // And and_1 has open pins: In_1=clock, In_2=not_1_out, out=open
  LED led_24 (.in(A1));
  LED led_25 (.in(A0));
  PullDown pulldown_21 (.out(A0));
  PullDown pulldown_22 (.out(A1));
  LED led_26 (.in(A3));
  LED led_27 (.in(A2));
  PullDown pulldown_23 (.out(A2));
  PullDown pulldown_24 (.out(A3));
  LED led_28 (.in(A5));
  LED led_29 (.in(A4));
  PullDown pulldown_25 (.out(A4));
  PullDown pulldown_26 (.out(A5));
  LED led_30 (.in(A7));
  LED led_31 (.in(A6));
  PullDown pulldown_27 (.out(A6));
  PullDown pulldown_28 (.out(A7));

  assign D0_2 = D0;
  assign D1_2 = D1;
  assign D2_2 = D2;
  assign D3_2 = D3;
  assign D4_2 = D4;
  assign D5_2 = D5;
  assign D6_2 = D6;
  assign D7_2 = D7;

  // Notes on the sheet:
  //   pipeline counter
  //   opcode counter
  //   Zero detector
  //   Address Bus
  //   FSM Bus
  //   tape control eeprom
  //   Decoder eeprom, translate a byte from ASCII into a valid BF instruction, ignores non valid;
  //   Code control eeprom, does  control logic of finite states for execute the current instruction;
  //   Tape control eeprom, selects which tape is active for use the Data bus and defines modes;
  //   Math operator eeprom, perform all math operations as table lookups;
  //   Data Bus
  //   Data Bus is shared by all tapes
  //   Basic Logic Level,
  //   check for fail states,
  //   does hold for swap tapes
  //   does hold for move direction
  //   could halt
endmodule
