// Digital circuit jelly-six.dig as structural Verilog
module jelly_six (
  input  clock,
  input  halt,
  input  D0,
  input  D1,
  input  D2,
  input  D3,
  input  D4,
  input  D5,
  input  D6,
  input  D7,
  output BOB,
  output ONE,
  output TWO,
  output RD,
  output WR,
  output FW,
  output BK,
  output HLT,
  output D0_2,
  output D1_2,
  output D2_2,
  output D3_2,
  output D4_2,
  output D5_2,
  output D6_2,
  output D7_2,
  output zero,
  output A0,
  output A1,
  output A2,
  output A3,
  output A4,
  output A5,
  output A6,
  output A7
);

  wire not_1_out, U1_p22, u5_pin11, u7_pin5, u7_pin12, u7_pin13, u8_pin3, u8_pin6, u8_pin8, u8_pin13,
       u9_pin3, u9_pin6;
  wire [1:0] U1_p14;
  wire [2:0] u6_pin11;
  wire [3:0] u3_p1;
  wire [7:0] u5_pin2, u5_pin19, u6_pin19;

  LED led_1 (.in(A0));
  LED led_2 (.in(A2));
  LED led_3 (.in(A1));
  LED led_4 (.in(A4));
  LED led_5 (.in(A3));
  LED led_6 (.in(A6));
  LED led_7 (.in(A5));
  LED led_8 (.in(A7));
  _74574 u5 (
    .pin1(1'b0), .pin2(u5_pin2[0]), .pin3(u5_pin2[1]), .pin4(u5_pin2[2]), .pin5(u5_pin2[3]),
    .pin6(u5_pin2[4]), .pin7(u5_pin2[5]), .pin8(u5_pin2[6]), .pin9(u5_pin2[7]), .pin10(1'b0),
    .pin11(u5_pin11), .pin12(u5_pin19[7]), .pin13(u5_pin19[6]), .pin14(u5_pin19[5]), .pin15(u5_pin19[4]),
    .pin16(u5_pin19[3]), .pin17(u5_pin19[2]), .pin18(u5_pin19[1]), .pin19(u5_pin19[0]), .pin20(1'b1));
  _74574 u6 (
    .pin1(1'b0), .pin2(u5_pin2[0]), .pin3(u5_pin2[1]), .pin4(u5_pin2[2]), .pin5(u5_pin2[3]),
    .pin6(u5_pin2[4]), .pin7(u5_pin2[5]), .pin8(u5_pin2[6]), .pin9(u5_pin2[7]), .pin10(1'b0),
    .pin11(u6_pin11[2]), .pin12(u6_pin19[7]), .pin13(u6_pin19[6]), .pin14(u6_pin19[5]), .pin15(u6_pin19[4]),
    .pin16(u6_pin19[3]), .pin17(u6_pin19[2]), .pin18(u6_pin19[1]), .pin19(u6_pin19[0]), .pin20(1'b1));
  // _28c16 U1: pin names not known; wires that end beside it: A7, A6, A5, A4, A3, A2, A1, A0, u6_pin11[0], u6_pin11[1], u6_pin11[2], 1'b0, 1'b1, U1_p14[0], U1_p14[1], 1'b1, 1'b0, 1'b0, 1'b0, U1_p14[1], U1_p14[0], U1_p22
  // _28c16 U2: pin names not known; wires that end beside it: A7, A6, A5, A4, A3, A2, A1, A0, BOB, ONE, TWO, 1'b0, 1'b1, U1_p14[0], U1_p14[1], 1'b1, U1_p22, 1'b0, 1'b0, HLT, BK, FW
  // _28c16 u3: pin names not known; wires that end beside it: u3_p1, u5_pin19[7], u5_pin19[6], u5_pin19[5], u5_pin19[4], u5_pin19[3], u5_pin19[2], u5_pin19[1], u5_pin19[0], u3_p1[0], u3_p1[1], u3_p1[2], 1'b0, 1'b1, 1'b0, 1'b0, 1'b1, 1'b0, 1'b0, 1'b0, A7, A6, A5
  // _28c16 u4: pin names not known; wires that end beside it: u6_pin19[7], u6_pin19[6], u6_pin19[5], u6_pin19[4], u6_pin19[3], u6_pin19[2], u6_pin19[1], u6_pin19[0], u5_pin2[0], u5_pin2[1], u5_pin2[2], 1'b0, 1'b1, u6_pin11[0], u6_pin11[1], 1'b1, 1'b0, 1'b0, 1'b0, u5_pin2[7], u5_pin2[6], u5_pin2[5]
  LED led_9 (.in(D0));
  LED led_10 (.in(ONE));
  LED led_11 (.in(BOB));
  LED led_12 (.in(D2));
  LED led_13 (.in(D1));
  LED led_14 (.in(RD));
  LED led_15 (.in(TWO));
  LED led_16 (.in(D4));
  LED led_17 (.in(D3));
  LED led_18 (.in(FW));
  LED led_19 (.in(WR));
  LED led_20 (.in(D6));
  LED led_21 (.in(D5));
  LED led_22 (.in(HLT));
  LED led_23 (.in(BK));
  _74193 u7 (
    .pin1(1'b0), .pin2(A1), .pin3(A0), .pin4(1'b1), .pin5(u7_pin5), .pin6(A2), .pin7(A3), .pin8(1'b0),
    .pin9(1'b0), .pin10(1'b0), .pin11(1'b1), .pin12(u7_pin12), .pin13(u7_pin13), .pin14(u5_pin11),
    .pin15(1'b0), .pin16(1'b1));
  LED led_24 (.in(D7));
  _7432 u8 (
    .pin1(u5_pin2[0]), .pin2(u5_pin2[1]), .pin3(u8_pin3), .pin4(u5_pin2[2]), .pin5(u5_pin2[3]),
    .pin6(u8_pin6), .pin7(1'b0), .pin8(u8_pin8), .pin9(u8_pin6), .pin10(u8_pin3), .pin11(zero),
    .pin12(u8_pin8), .pin13(u8_pin13), .pin14(1'b1));
  _7432 u9 (
    .pin1(u5_pin2[4]), .pin2(u5_pin2[5]), .pin3(u9_pin3), .pin4(u5_pin2[6]), .pin5(u5_pin2[7]),
    .pin6(u9_pin6), .pin7(1'b0), .pin8(u8_pin13), .pin9(u9_pin6), .pin10(u9_pin3), .pin12(1'b1),
    .pin13(1'b1), .pin14(1'b1));  // open: pin11
  LED led_25 (.in(u7_pin13));
  LED led_26 (.in(u7_pin12));
  LED led_27 (.in(D1));
  LED led_28 (.in(D0));
  LED led_29 (.in(u5_pin11));
  LED led_30 (.in(D3));
  LED led_31 (.in(D2));
  LED led_32 (.in(clock));
  not not_1 (not_1_out, halt);
  LED led_33 (.in(zero));
  LED led_34 (.in(D5));
  LED led_35 (.in(D4));
  LED led_36 (.in(not_1_out));
  and and_1 (u7_pin5, clock, not_1_out);
  LED led_37 (.in(D7));
  LED led_38 (.in(D6));

  assign D0_2 = D0;
  assign D1_2 = D1;
  assign D2_2 = D2;
  assign D3_2 = D3;
  assign D4_2 = D4;
  assign D5_2 = D5;
  assign D6_2 = D6;
  assign D7_2 = D7;

  // Notes on the sheet:
  //   Data Bus
  //   FSM Bus
  //   code control eeprom
  //   tape control eeprom
  //   decoder eeprom
  //   lookup math eeprom
  //   Device Control
  //   Zero detector
  //   pipeline counter
endmodule
