// Digital circuit jelly-two-halt.dig as structural Verilog
module jelly_two_halt (
  input  rd,
  input  wr,
  input  bob,
  input  one,
  input  two,
  input  swap,
  input  fw,
  input  bk,
  input  move,
  input  rd_2,
  input  wr_2,
  input  fw_3,
  input  bk_3,
  output halt,
  output BOB_2,
  output bob_one_two,
  output bob_one,
  output bob_two,
  output one_two,
  output ONE_2,
  output TWO_2,
  output FW_2,
  output BK_2,
  output RD_3,
  output WR_3
);

  wire and_3_out, and_4_out, and_9_out, and_10_out, and_11_out, and_12_out, and_13_out, and_14_out, d_ff_1_q,
       d_ff_2_q, nand_1_out, or_1_out, or_2_out, or_3_out, or_4_out, or_5_out, or_6_out, or_7_out, or_8_out,
       xor_1_out, xor_2_out, xor_3_out, xor_4_out, xor_5_out, xor_6_out, xor_7_out;

  xor xor_1 (xor_1_out, rd_2, wr_2);
  xor xor_2 (xor_2_out, d_ff_1_q, 1'b1);
  xor xor_3 (xor_3_out, one, two);
  xor xor_4 (xor_4_out, and_3_out, one);
  xor xor_5 (xor_5_out, and_3_out, two);
  xor xor_6 (xor_6_out, d_ff_2_q, 1'b1);
  xor xor_7 (xor_7_out, fw, bk);
  xor xor_8 (FW_2, and_4_out, fw);
  xor xor_9 (BK_2, and_4_out, bk);
  and and_1 (RD_3, xor_1_out, rd_2);
  and and_2 (WR_3, xor_1_out, wr_2);
  D_FF d_ff_1 (.D(xor_2_out), .C(swap), .Q(d_ff_1_q));  // open: nQ
  and and_3 (and_3_out, d_ff_1_q, xor_3_out);
  D_FF d_ff_2 (.D(xor_6_out), .C(move), .Q(d_ff_2_q));  // open: nQ
  and and_4 (and_4_out, d_ff_2_q, xor_7_out);
  and and_5 (bob_one, bob, one);
  and and_6 (bob_two, bob, two);
  and and_7 (one_two, one, two);
  and and_8 (bob_one_two, bob_one, bob_two);
  and and_9 (and_9_out, rd, wr);
  and and_10 (and_10_out, fw_3, bk_3);
  and and_11 (and_11_out, rd, bk_3);
  and and_12 (and_12_out, rd, fw_3);
  and and_13 (and_13_out, wr, bk_3);
  and and_14 (and_14_out, wr, fw_3);
  or or_1 (or_1_out, bob_one_two, bob_one);
  or or_2 (or_2_out, bob_two, one_two);
  or or_3 (or_3_out, and_9_out, and_10_out);
  or or_4 (or_4_out, and_11_out, and_12_out);
  or or_5 (or_5_out, and_13_out, and_14_out);
  or or_6 (or_6_out, or_1_out, or_2_out);
  and and_15 (BOB_2, bob, nand_1_out);
  and and_16 (ONE_2, xor_4_out, nand_1_out);
  and and_17 (TWO_2, xor_5_out, nand_1_out);
  or or_7 (or_7_out, or_4_out, or_5_out);
  nand nand_1 (nand_1_out, or_6_out, or_6_out);
  or or_8 (or_8_out, or_3_out, or_7_out);
  and and_18 (halt, nand_1_out, or_8_out);
endmodule
